# Fritzing sketch arduino-nodemcu_OjnaKz5IO1 (saved by Fritzing 0.9.3b)

parts:
  U1 = NodeMCU V1.0
  Part1 = Arduino Uno (Rev3)
  AM1 = AM2320 Humidity and Temperature Sensor [part_number="Adafruit #3721"]

nets:
  GND: U1.GND, Part1.GND, AM1.SCL
  N1: U1.RX, Part1.D3_PWM
  N2: U1.TX, Part1.D2
  N3: Part1.A0, AM1.SDA
  5V: Part1.5V, AM1.VDD

notes:
  Arduino UNO
  ESP8266-12(NODE MCU)
  DHT11
  Humidity & Temperature sensor

custom parts:
  NodeMCU V1.0: ESP8266 based NodeMCU
  AM2320 Humidity and Temperature Sensor: AM2320 I2C Humidity and Temperature Sensor
